// Logisim project arch242.circ as structural Verilog: 11 circuits, main circuit main
module main (
);

  wire ACCWrite, c_out, Carry, cf, CFWrite, clk, clock_1_out, controlled_buffer_1_out, DataSrc, DualWrite,
       funct, Halt, InstrSrc, IsSupported, MemSrc, MemWrite, NOP, not_1_out, not_2_out, RegWrite, TEMPWrite,
       WriteCF, Zero;
  wire [1:0] ALUSrcA, CFSrc, ImmSrc, RotSrc, TEMPSrc;
  wire [2:0] ALUControl, ALUSrcB, multiplexer_3_out, multiplexer_4_out, PCSrc, RegSrc, ResultSrc;
  wire [3:0] acc, ALUResult, bit_extender_1_out, MemRD, MemWD, RegRD, Result, rotacc, SrcA, SrcB;
  wire [7:0] instrmem_1_instr1, instrmem_1_instr2, MemAddr, RB_RA, RD_RC;
  wire [10:0] BranchImm;
  wire [11:0] PCTemp;
  wire [11:11] Imm12bit;
  wire [15:0] Instr, PC, PCNext, PCPlus1, PCPlus2, WriteTEMP;
  wire [15:12] TEMP;

  // Probe on {Instr[15:13], funct, Instr[11:0]}
  LED led_1 (.in(IsSupported));
  Clock clock_1 (.out(clock_1_out));
  assign controlled_buffer_1_out = not_1_out ? clock_1_out : 1'bz;  // Controlled_Buffer controlled_buffer_1
  not not_1 (not_1_out, Halt);
  Register #(.width(16)) u_PC (.D(PCNext), .clk(controlled_buffer_1_out), .Q(PC));  // open: en, clr
  assign clk = not_2_out ? controlled_buffer_1_out : 1'bz;  // Controlled_Buffer controlled_buffer_2
  not not_2 (not_2_out, NOP);
  // Probe on PCSrc
  Adder #(.width(16)) adder_1 (.a(PC), .b(16'h1), .out(PCPlus1));  // open: cin, cout
  // Probe on PCNext
  Multiplexer #(.select(3), .width(16)) multiplexer_1 (
    .in0(PCPlus1), .in1(PCPlus2), .in2({PC[15:12], PCTemp}), .in3({PC[15:11], BranchImm}),
    .in4({PC[15:12], Imm12bit[11], BranchImm}), .out(PCNext), .sel(PCSrc));  // open: in5, in6, in7
  Adder #(.width(16)) adder_2 (.a(PC), .b(16'h2), .out(PCPlus2));  // open: cin, cout
  // Probe on {PC[15:11], BranchImm}
  // Probe on {PC[15:12], Imm12bit[11], BranchImm}
  maindec maindec_1 (
    .Instr({Instr[15:13], funct, Instr[11:0]}), .ACC(acc), .CF(cf), .InstrSrc(InstrSrc), .Zero(Zero),
    .IsSupported(IsSupported), .RegWrite(RegWrite), .ACCWrite(ACCWrite), .MemWrite(MemWrite),
    .ResultSrc(ResultSrc), .CFWrite(CFWrite), .DataSrc(DataSrc), .MemSrc(MemSrc), .ALUSrcA(ALUSrcA),
    .ALUSrcB(ALUSrcB), .ImmSrc(ImmSrc), .CFSrc(CFSrc), .NOP(NOP), .RegSrc(RegSrc), .PCSrc(PCSrc),
    .TEMPSrc(TEMPSrc), .TEMPWrite(TEMPWrite), .Halt(Halt), .Carry(Carry), .DualRegWrite(DualWrite),
    .RotSrc(RotSrc));
  aludec aludec_1 (.opcode({Instr[15:13], funct, Instr[11:8]}), .ALUControl(ALUControl));
  // Probe on instrmem_1_instr1
  instrmem instrmem_1 (.A1(PC), .A2(PCPlus1), .instr1(instrmem_1_instr1), .Instr2(instrmem_1_instr2));
  // Probe on instrmem_1_instr2
  LED led_2 (.in(IsSupported));
  // Probe on ALUControl
  immdec immdec_1 (.Instr({Instr[15:13], funct, Instr[11:0]}), .ImmSrc(ImmSrc), .Imm11_0({Imm12bit[11], BranchImm}));
  Multiplexer #(.width(16)) multiplexer_2 (
    .in0({instrmem_1_instr1, {8{1'b0}}}), .in1({instrmem_1_instr1, instrmem_1_instr2}),
    .out({Instr[15:13], funct, Instr[11:0]}), .sel(InstrSrc));
  // Probe on BranchImm[3:0]
  // Probe on BranchImm
  // Probe on {Imm12bit[11], BranchImm}
  // Probe on RegWrite
  // Probe on ACCWrite
  // Probe on MemWrite
  // Probe on ResultSrc
  // Probe on CFWrite
  // Probe on DataSrc
  // Probe on MemSrc
  // Probe on ALUSrcA
  // Probe on ALUSrcB
  // Probe on ImmSrc
  // Probe on CFSrc
  // Probe on NOP
  // Probe on RegSrc
  // Probe on PCSrc
  // Probe on TEMPSrc
  // Probe on TEMPWrite
  // Probe on Halt
  // Probe on Carry
  // Probe on DualWrite
  // Probe on RotSrc
  instrlengthdec instrlengthdec_1 (.instr(instrmem_1_instr1), .is2Byte(InstrSrc));
  Multiplexer #(.width(3)) multiplexer_3 (.in0(3'b011), .in1(3'b001), .out(multiplexer_3_out), .sel(funct));
  // Probe on multiplexer_3_out
  Register #(.width(4)) u_ACC (.D(Result), .en(ACCWrite), .clk(clk), .Q(acc));  // open: clr
  Register #(.width(1)) u_CF (.D(WriteCF), .en(CFWrite), .clk(clk), .Q(cf));  // open: clr
  Register #(.width(16)) u_TEMP (.D(WriteTEMP), .en(TEMPWrite), .clk(clk), .Q({TEMP, PCTemp}));  // open: clr
  Multiplexer #(.select(3), .width(3)) multiplexer_4 (
    .in0(3'b000), .in1(3'b001), .in2(3'b010), .in3(3'b011), .in4(3'b100), .in5(Instr[11:9]),
    .out(multiplexer_4_out), .sel(RegSrc));  // open: in6, in7
  // Probe on multiplexer_4_out
  Multiplexer #(.select(2)) multiplexer_5 (
    .in0(cf), .in1(c_out), .in2(Instr[8]), .in3(1'b1), .out(WriteCF), .sel(CFSrc));
  // Probe on RegRD
  regfile regfile_1 (
    .A1(multiplexer_4_out), .A2(multiplexer_4_out), .A3(multiplexer_3_out), .WD(Result), .WE(RegWrite),
    .DualWD({Imm12bit[11], BranchImm}), .DualWE(DualWrite), .CLK(clk), .ReadData(RegRD), .RB_RA(RB_RA),
    .RD_RC(RD_RC));
  // Probe on WriteCF
  // Probe on WriteTEMP
  Multiplexer #(.select(2), .width(16)) multiplexer_6 (
    .in0({TEMP, PCTemp}), .in1({16{1'b0}}), .in2(PCPlus2), .out(WriteTEMP), .sel(TEMPSrc));  // open: in3
  // Probe on SrcA
  // Probe on SrcB
  assign bit_extender_1_out = {{3{cf}}, cf};  // Bit_Extender bit_extender_1
  Multiplexer #(.select(2), .width(4)) multiplexer_7 (
    .in0(acc), .in1(MemRD), .in2(RegRD), .in3(bit_extender_1_out), .out(SrcA), .sel(ALUSrcA));
  // Probe on SrcB
  Multiplexer #(.select(3), .width(4)) multiplexer_8 (
    .in0(4'b0000), .in1(MemRD), .in2(4'b0001), .in3(BranchImm[3:0]), .in4(4'b0110), .out(SrcB), .sel(ALUSrcB));  // open: in5, in6, in7
  // Probe on ALUResult
  alu alu_1 (
    .SrcA(SrcA), .SrcB(SrcB), .ALUControl(ALUControl), .CarryIn(cf), .CarryEnable(Carry), .Zero(Zero),
    .ALUResult(ALUResult), .CarryOut(c_out));
  // Probe on rotacc
  rotate rotate_1 (.ACCIn(acc), .cfIn(cf), .RotSrc(RotSrc), .accOut(rotacc));
  // Probe on MemAddr
  // Probe on MemWD
  Multiplexer #(.width(8)) multiplexer_9 (.in0(RB_RA), .in1(RD_RC), .out(MemAddr), .sel(MemSrc));
  Multiplexer #(.width(4)) multiplexer_10 (.in0(acc), .in1(ALUResult), .out(MemWD), .sel(DataSrc));
  // Probe on MemRD
  datamem datamem_1 (.A(MemAddr), .WE(MemWrite), .WD(MemWD), .clk(clk), .RD(MemRD));
  // Probe on Result
  Multiplexer #(.select(3), .width(4)) multiplexer_11 (
    .in0(ALUResult), .in1(MemRD), .in2(RegRD), .in3(BranchImm[3:0]), .in4(acc), .in5(rotacc), .out(Result),
    .sel(ResultSrc));  // open: in6, in7

  // Other names for the same wires on the sheet: opcode[7:0] = {Instr[15:13], funct, Instr[11:8]}; setcf = Instr[8];
  //   rs[2:0] = Instr[11:9]; Instr[12] = funct; PCTarget1[15:0] = {PC[15:11], BranchImm}; Imm[3:0] = BranchImm[3:0];
  //   Imm12bit[10:0] = BranchImm; PCTarget2[15:0] = {PC[15:12], Imm12bit[11], BranchImm}; PCTemp[15:12] = PC[15:12];
  //   TEMP[11:0] = PCTemp; TEMP12_0[11:0] = PCTemp

  // Notes on the sheet:
  //   Instruction Decoder
  //   Control Unit
  //   Instruction Memory
  //   Immediate Decoder
  //   RegFile
  //   Special Registers
  //   ALU
  //   Rotate
  //   Data Memory
  //   WriteBack
endmodule

module maindec (
  input  [15:0] Instr,
  input  [3:0] ACC,
  input  CF,
  input  InstrSrc,
  input  Zero,
  output IsSupported,
  output RegWrite,
  output ACCWrite,
  output MemWrite,
  output [2:0] ResultSrc,
  output CFWrite,
  output DataSrc,
  output MemSrc,
  output [1:0] ALUSrcA,
  output [2:0] ALUSrcB,
  output [1:0] ImmSrc,
  output [1:0] CFSrc,
  output NOP,
  output [2:0] RegSrc,
  output [2:0] PCSrc,
  output [1:0] TEMPSrc,
  output TEMPWrite,
  output Halt,
  output Carry,
  output DualRegWrite,
  output [1:0] RotSrc
);

  wire and_5_out, and_9_out, and_10_out, and_11_out, BBitCond, BCDCond, BEQZ, Branch, comparator_5_gt,
       comparator_6_lt, comparator_7_eq, comparator_8_eq, comparator_9_eq, comparator_10_eq,
       comparator_11_eq, comparator_12_lt, comparator_13_gt, comparator_14_lt, comparator_15_gt,
       comparator_16_lt, comparator_17_eq, comparator_18_lt, comparator_20_gt, comparator_21_lt,
       comparator_22_eq, comparator_24_eq, comparator_25_eq, comparator_26_eq, comparator_27_eq,
       comparator_30_eq, comparator_31_eq, comparator_34_eq, comparator_35_eq, comparator_36_eq,
       comparator_37_eq, comparator_44_eq, comparator_45_eq, comparator_46_eq, comparator_47_eq,
       comparator_48_eq, comparator_49_eq, comparator_50_eq, comparator_51_gt, IsACCImm, IsAdd_Sub,
       IsALUImmOp, IsALUtoACC, IsALUtoMem, IsB, IsBBit, IsBCD, IsBEQZ, IsBEQZ_cf, IsBNZ_a, IsBNZ_b, IsBNZ_d,
       IsCall, IsFrom_mba, IsFrom_mdc, IsFrom_reg, IsIncDec_acc, IsIncDec_mba, IsIncDec_mdc, IsIncDec_reg,
       IsR4Imm, IsRARB, IsRCRD, IsRet, IsRotate, IsRotateCF, IsSetCF, IsTo_mba, IsTo_mdc, IsTo_reg,
       multiplexer_8_out, not_1_out, not_2_out, not_3_out, not_4_out, not_5_out, priority_encoder_1_en_out;
  wire [2:0] multiplexer_7_out, PCSrc_t;
  wire [4:0] Selector;

  Comparator #(.mode("unsigned")) comparator_1 (.a(Instr[15:8]), .b(8'h4), .eq(IsFrom_mba));  // open: gt, lt
  Comparator #(.mode("unsigned")) comparator_2 (.a(Instr[15:8]), .b(8'h5), .eq(IsTo_mba));  // open: gt, lt
  Comparator #(.mode("unsigned")) comparator_3 (.a(Instr[15:8]), .b(8'h6), .eq(IsFrom_mdc));  // open: gt, lt
  Comparator #(.mode("unsigned")) comparator_4 (.a(Instr[15:8]), .b(8'h7), .eq(IsTo_mdc));  // open: gt, lt
  Comparator #(.mode("unsigned")) comparator_5 (.a(Instr[15:8]), .b(8'h7), .gt(comparator_5_gt));  // open: eq, lt
  Comparator #(.mode("unsigned")) comparator_6 (.a(Instr[15:8]), .b(8'hc), .lt(comparator_6_lt));  // open: gt, eq
  Comparator #(.mode("unsigned")) comparator_7 (.a(Instr[15:8]), .b(8'hc), .eq(comparator_7_eq));  // open: gt, lt
  Comparator #(.mode("unsigned")) comparator_8 (.a(Instr[15:8]), .b(8'hd), .eq(comparator_8_eq));  // open: gt, lt
  Comparator #(.mode("unsigned")) comparator_9 (.a(Instr[15:8]), .b(8'he), .eq(comparator_9_eq));  // open: gt, lt
  Comparator #(.mode("unsigned")) comparator_10 (.a(Instr[15:8]), .b(8'hf), .eq(comparator_10_eq));  // open: gt, lt
  Comparator #(.mode("unsigned"), .width(4)) comparator_11 (
    .a(Instr[15:12]), .b(4'b0001), .eq(comparator_11_eq));  // open: gt, lt
  Comparator #(.mode("unsigned"), .width(3)) comparator_12 (
    .a(Instr[11:9]), .b(3'b101), .lt(comparator_12_lt));  // open: gt, eq
  Comparator #(.mode("unsigned")) comparator_13 (.a(Instr[15:8]), .b(8'h19), .gt(comparator_13_gt));  // open: eq, lt
  Comparator #(.mode("unsigned")) comparator_14 (.a(Instr[15:8]), .b(8'h1d), .lt(comparator_14_lt));  // open: gt, eq
  Comparator #(.mode("unsigned")) comparator_15 (.a(Instr[15:8]), .b(8'h1c), .gt(comparator_15_gt));  // open: eq, lt
  Comparator #(.mode("unsigned")) comparator_16 (.a(Instr[15:8]), .b(8'h20), .lt(comparator_16_lt));  // open: gt, eq
  Comparator #(.mode("unsigned"), .width(4)) comparator_17 (
    .a(Instr[15:12]), .b(4'b0010), .eq(comparator_17_eq));  // open: gt, lt
  Comparator #(.mode("unsigned"), .width(3)) comparator_18 (
    .a(Instr[11:9]), .b(3'b101), .lt(comparator_18_lt));  // open: gt, eq
  Comparator #(.mode("unsigned"), .width(7)) comparator_19 (
    .a(Instr[15:9]), .b(7'b0010101), .eq(IsSetCF));  // open: gt, lt
  Comparator #(.mode("unsigned")) comparator_20 (.a(Instr[15:8]), .b(8'h3f), .gt(comparator_20_gt));  // open: eq, lt
  Comparator #(.mode("unsigned")) comparator_21 (.a(Instr[15:8]), .b(8'h45), .lt(comparator_21_lt));  // open: gt, eq
  Comparator #(.mode("unsigned"), .width(4)) comparator_22 (
    .a(Instr[7:4]), .b(4'b0000), .eq(comparator_22_eq));  // open: gt, lt
  Comparator #(.mode("unsigned")) comparator_23 (.a(Instr[15:8]), .b(8'h46), .eq(IsR4Imm));  // open: gt, lt
  Comparator #(.mode("unsigned")) comparator_24 (
    .a(Instr[15:8]), .b({8{1'b0}}), .eq(comparator_24_eq));  // open: gt, lt
  Comparator #(.mode("unsigned")) comparator_25 (.a(Instr[15:8]), .b(8'h1), .eq(comparator_25_eq));  // open: gt, lt
  Comparator #(.mode("unsigned")) comparator_26 (.a(Instr[15:8]), .b(8'h2), .eq(comparator_26_eq));  // open: gt, lt
  Comparator #(.mode("unsigned")) comparator_27 (.a(Instr[15:8]), .b(8'h3), .eq(comparator_27_eq));  // open: gt, lt
  Comparator #(.mode("unsigned"), .width(4)) comparator_28 (
    .a(Instr[15:12]), .b(4'b0111), .eq(IsACCImm));  // open: gt, lt
  Comparator #(.mode("unsigned")) comparator_29 (.a(Instr[15:8]), .b(8'h2e), .eq(IsRet));  // open: gt, lt
  Comparator #(.mode("unsigned")) comparator_30 (.a(Instr[15:8]), .b(8'h31), .eq(comparator_30_eq));  // open: gt, lt
  Comparator #(.mode("unsigned")) comparator_31 (.a(Instr[15:8]), .b(8'h3f), .eq(comparator_31_eq));  // open: gt, lt
  Comparator #(.mode("unsigned"), .width(5)) comparator_32 (
    .a(Instr[15:11]), .b(5'b10100), .eq(IsBNZ_a));  // open: gt, lt
  Comparator #(.mode("unsigned"), .width(5)) comparator_33 (
    .a(Instr[15:11]), .b(5'b10101), .eq(IsBNZ_b));  // open: gt, lt
  Comparator #(.mode("unsigned"), .width(5)) comparator_34 (
    .a(Instr[15:11]), .b(5'b10110), .eq(comparator_34_eq));  // open: gt, lt
  Comparator #(.mode("unsigned"), .width(5)) comparator_35 (
    .a(Instr[15:11]), .b(5'b10111), .eq(comparator_35_eq));  // open: gt, lt
  Comparator #(.mode("unsigned"), .width(5)) comparator_36 (
    .a(Instr[15:11]), .b(5'b11000), .eq(comparator_36_eq));  // open: gt, lt
  Comparator #(.mode("unsigned"), .width(5)) comparator_37 (
    .a(Instr[15:11]), .b(5'b11001), .eq(comparator_37_eq));  // open: gt, lt
  Comparator #(.mode("unsigned"), .width(5)) comparator_38 (
    .a(Instr[15:11]), .b(5'b11011), .eq(IsBNZ_d));  // open: gt, lt
  Comparator #(.mode("unsigned"), .width(4)) comparator_39 (.a(Instr[15:12]), .b(4'b1110), .eq(IsB));  // open: gt, lt
  Comparator #(.mode("unsigned"), .width(4)) comparator_40 (
    .a(Instr[15:12]), .b(4'b1111), .eq(IsCall));  // open: gt, lt
  Comparator #(.mode("unsigned")) comparator_41 (.a(Instr[15:8]), .b(8'h36), .eq(IsBCD));  // open: gt, lt
  Comparator #(.mode("unsigned"), .width(16)) comparator_42 (.a(Instr), .b(16'h373e), .eq(Halt));  // open: gt, lt
  Comparator #(.mode("unsigned"), .width(3)) comparator_43 (.a(Instr[15:13]), .b(3'b100), .eq(IsBBit));  // open: gt, lt
  Comparator #(.mode("unsigned"), .width(4)) comparator_44 (
    .a(Instr[15:12]), .b(4'b0101), .eq(comparator_44_eq));  // open: gt, lt
  Comparator #(.mode("unsigned"), .width(4)) comparator_45 (
    .a(Instr[7:4]), .b(4'b0000), .eq(comparator_45_eq));  // open: gt, lt
  Comparator #(.mode("unsigned"), .width(4)) comparator_46 (
    .a(Instr[15:12]), .b(4'b0110), .eq(comparator_46_eq));  // open: gt, lt
  Comparator #(.mode("unsigned"), .width(4)) comparator_47 (
    .a(Instr[7:4]), .b(4'b0000), .eq(comparator_47_eq));  // open: gt, lt
  and and_1 (IsAdd_Sub, comparator_5_gt, comparator_6_lt);
  or or_1 (IsIncDec_mba, comparator_7_eq, comparator_8_eq);
  or or_2 (IsIncDec_mdc, comparator_9_eq, comparator_10_eq);
  and and_2 (IsIncDec_reg, comparator_11_eq, comparator_12_lt);
  and and_3 (IsALUtoACC, comparator_13_gt, comparator_14_lt);
  and and_4 (IsALUtoMem, comparator_15_gt, comparator_16_lt);
  and and_5 (and_5_out, comparator_17_eq, comparator_18_lt);
  Decoder decoder_1 (.out0(IsTo_reg), .out1(IsFrom_reg), .sel(Instr[8]), .en(and_5_out));
  and and_6 (IsALUImmOp, comparator_20_gt, comparator_21_lt, comparator_22_eq);
  or or_3 (IsRotate, comparator_24_eq, comparator_25_eq);
  or or_4 (IsRotateCF, comparator_26_eq, comparator_27_eq);
  or or_5 (IsIncDec_acc, comparator_30_eq, comparator_31_eq);
  or or_6 (IsBEQZ, comparator_34_eq, comparator_35_eq);
  or or_7 (IsBEQZ_cf, comparator_36_eq, comparator_37_eq);
  and and_7 (IsRARB, comparator_44_eq, comparator_45_eq);
  and and_8 (IsRCRD, comparator_46_eq, comparator_47_eq);
  Comparator #(.mode("unsigned"), .width(5)) comparator_48 (
    .a(Instr[15:11]), .b(5'b10110), .eq(comparator_48_eq));  // open: gt, lt
  Comparator #(.mode("unsigned"), .width(5)) comparator_49 (
    .a(Instr[15:11]), .b(5'b11000), .eq(comparator_49_eq));  // open: gt, lt
  Multiplexer #(.select(5)) multiplexer_1 (
    .in0(1'b0), .in1(1'b0), .in2(1'b0), .in3(1'b0), .in4(1'b1), .in5(1'b0), .in6(1'b0), .in7(1'b0),
    .in8(1'b1), .in9(1'b0), .in10(1'b0), .in11(1'b1), .in12(1'b0), .in13(1'b1), .in14(1'b0), .in15(1'b0),
    .in16(1'b1), .in17(1'b0), .in18(1'b0), .in19(1'b0), .in20(1'b0), .in21(1'b0), .in22(1'b0), .in23(1'b0),
    .in24(1'b0), .in25(1'b0), .in26(1'b0), .in27(1'b0), .in28(1'b0), .in29(1'b0), .in30(1'b0), .in31(1'b0),
    .out(RegWrite), .sel(Selector));
  Multiplexer #(.select(5)) multiplexer_2 (
    .in0(1'b0), .in1(1'b1), .in2(1'b0), .in3(1'b1), .in4(1'b0), .in5(1'b0), .in6(1'b1), .in7(1'b1),
    .in8(1'b0), .in9(1'b0), .in10(1'b1), .in11(1'b0), .in12(1'b0), .in13(1'b0), .in14(1'b0), .in15(1'b0),
    .in16(1'b0), .in17(1'b0), .in18(1'b0), .in19(1'b0), .in20(1'b0), .in21(1'b0), .in22(1'b0), .in23(1'b0),
    .in24(1'b0), .in25(1'b0), .in26(1'b0), .in27(1'b0), .in28(1'b0), .in29(1'b0), .in30(1'b0), .in31(1'b0),
    .out(MemWrite), .sel(Selector));
  Multiplexer #(.select(5)) multiplexer_3 (
    .in0(1'b0), .in1(1'b0), .in2(1'b0), .in3(1'b0), .in4(1'b0), .in5(1'b0), .in6(1'b1), .in7(1'b1),
    .in8(1'b0), .in9(1'b0), .in10(1'b1), .in11(1'b0), .in12(1'b0), .in13(1'b0), .in14(1'b0), .in15(1'b0),
    .in16(1'b0), .in17(1'b0), .in18(1'b0), .in19(1'b0), .in20(1'b0), .in21(1'b0), .in22(1'b0), .in23(1'b0),
    .in24(1'b0), .in25(1'b0), .in26(1'b0), .in27(1'b0), .in28(1'b0), .in29(1'b0), .in30(1'b0), .in31(1'b0),
    .out(DataSrc), .sel(Selector));
  or or_8 (BEQZ, comparator_48_eq, comparator_49_eq);
  or or_9 (Branch, IsBNZ_a, IsBNZ_b, IsBEQZ_cf, IsBNZ_d, IsBEQZ, IsBBit);
  Multiplexer #(.select(5)) multiplexer_4 (
    .in0(1'b1), .in1(1'b0), .in2(1'b1), .in3(1'b0), .in4(1'b1), .in5(1'b1), .in6(1'b0), .in7(1'b0),
    .in8(1'b0), .in9(1'b1), .in10(1'b0), .in11(1'b0), .in12(1'b1), .in13(1'b0), .in14(1'b0), .in15(1'b1),
    .in16(1'b0), .in17(1'b1), .in18(1'b1), .in19(1'b0), .in20(1'b1), .in21(1'b0), .in22(1'b1), .in23(1'b0),
    .in24(1'b0), .in25(1'b0), .in26(1'b0), .in27(1'b0), .in28(1'b0), .in29(1'b0), .in30(1'b1), .in31(1'b0),
    .out(ACCWrite), .sel(Selector));
  Multiplexer #(.select(5), .width(3)) multiplexer_5 (
    .in0(3'b001), .in1(3'b100), .in2(3'b001), .in3(3'b100), .in4(3'b000), .in5(3'b000), .in6(3'b000),
    .in7(3'b000), .in8(3'b000), .in9(3'b000), .in10(3'b000), .in11(3'b100), .in12(3'b010), .in13(3'b100),
    .in14(3'b100), .in15(3'b000), .in16(3'b011), .in17(3'b101), .in18(3'b101), .in19(3'b100), .in20(3'b011),
    .in21(3'b100), .in22(3'b000), .in23(3'b100), .in24(3'b100), .in25(3'b100), .in26(3'b100), .in27(3'b100),
    .in28(3'b100), .in29(3'b100), .in30(3'b000), .in31(3'b100), .out(ResultSrc), .sel(Selector));
  Multiplexer #(.select(5)) multiplexer_6 (
    .in0(1'b0), .in1(1'b0), .in2(1'b1), .in3(1'b1), .in4(1'b0), .in5(1'b0), .in6(1'b0), .in7(1'b1),
    .in8(1'b0), .in9(1'b0), .in10(1'b0), .in11(1'b0), .in12(1'b0), .in13(1'b0), .in14(1'b0), .in15(1'b0),
    .in16(1'b0), .in17(1'b0), .in18(1'b0), .in19(1'b0), .in20(1'b0), .in21(1'b0), .in22(1'b0), .in23(1'b0),
    .in24(1'b0), .in25(1'b0), .in26(1'b0), .in27(1'b0), .in28(1'b0), .in29(1'b0), .in30(1'b0), .in31(1'b0),
    .out(MemSrc), .sel(Selector));
  not not_1 (not_1_out, BCDCond);
  not not_2 (not_2_out, BBitCond);
  Multiplexer #(.width(3)) multiplexer_7 (.in0(3'b000), .in1(3'b001), .out(multiplexer_7_out), .sel(InstrSrc));
  Multiplexer multiplexer_8 (.in0(Zero), .in1(not_3_out), .out(multiplexer_8_out), .sel(BEQZ));
  not not_3 (not_3_out, Zero);
  Comparator #(.mode("unsigned")) comparator_50 (.a(Instr[15:8]), .b(8'h3e), .eq(comparator_50_eq));  // open: gt, lt
  and and_9 (and_9_out, not_1_out, IsBCD);
  and and_10 (and_10_out, not_2_out, IsBBit);
  Comparator #(.mode("unsigned"), .width(4)) comparator_51 (
    .a(ACC), .b(4'b1001), .gt(comparator_51_gt));  // open: eq, lt
  Multiplexer #(.select(2)) multiplexer_9 (
    .in0(ACC[0]), .in1(ACC[1]), .in2(ACC[2]), .in3(ACC[3]), .out(BBitCond), .sel(Instr[12:11]));
  // Probe on Instr[12:11]
  Multiplexer #(.width(3)) multiplexer_10 (.in0(PCSrc_t), .in1(multiplexer_7_out), .out(PCSrc), .sel(and_11_out));
  and and_11 (and_11_out, multiplexer_8_out, Branch);
  not not_4 (not_4_out, priority_encoder_1_en_out);
  // Probe on Selector
  Priority_Encoder #(.select(5)) priority_encoder_1 (
    .in0(IsFrom_mba), .in1(IsTo_mba), .in2(IsFrom_mdc), .in3(IsTo_mdc), .in4(IsRARB), .in5(IsAdd_Sub),
    .in6(IsIncDec_mba), .in7(IsIncDec_mdc), .in8(IsIncDec_reg), .in9(IsALUtoACC), .in10(IsALUtoMem),
    .in11(IsTo_reg), .in12(IsFrom_reg), .in13(IsRCRD), .in14(IsSetCF), .in15(IsALUImmOp), .in16(IsR4Imm),
    .in17(IsRotate), .in18(IsRotateCF), .in19(NOP), .in20(IsACCImm), .in21(IsRet), .in22(IsIncDec_acc),
    .in23(IsBNZ_a), .in24(IsBNZ_b), .in25(IsBEQZ), .in26(IsBEQZ_cf), .in27(IsBNZ_d), .in28(IsB),
    .in29(IsCall), .in30(IsBCD), .in31(IsBBit), .out(Selector), .en_out(priority_encoder_1_en_out));  // open: gs, en_in
  or or_10 (BCDCond, comparator_51_gt, CF);
  or or_11 (IsSupported, not_4_out, Halt);
  Multiplexer #(.select(5)) multiplexer_11 (
    .in0(1'b0), .in1(1'b0), .in2(1'b0), .in3(1'b0), .in4(1'b1), .in5(1'b1), .in6(1'b0), .in7(1'b0),
    .in8(1'b0), .in9(1'b0), .in10(1'b0), .in11(1'b0), .in12(1'b0), .in13(1'b1), .in14(1'b1), .in15(1'b1),
    .in16(1'b0), .in17(1'b0), .in18(1'b1), .in19(1'b0), .in20(1'b0), .in21(1'b0), .in22(1'b0), .in23(1'b0),
    .in24(1'b0), .in25(1'b0), .in26(1'b0), .in27(1'b0), .in28(1'b0), .in29(1'b0), .in30(1'b1), .in31(1'b0),
    .out(CFWrite), .sel(Selector));
  Multiplexer #(.select(5), .width(2)) multiplexer_12 (
    .in0(2'b00), .in1(2'b00), .in2(2'b00), .in3(2'b00), .in4(2'b01), .in5(2'b01), .in6(2'b00), .in7(2'b00),
    .in8(2'b00), .in9(2'b00), .in10(2'b00), .in11(2'b00), .in12(2'b00), .in13(2'b10), .in14(2'b10),
    .in15(2'b01), .in16(2'b00), .in17(2'b00), .in18(2'b01), .in19(2'b00), .in20(2'b00), .in21(2'b00),
    .in22(2'b00), .in23(2'b00), .in24(2'b00), .in25(2'b00), .in26(2'b00), .in27(2'b00), .in28(2'b00),
    .in29(2'b00), .in30(2'b11), .in31(2'b00), .out(CFSrc), .sel(Selector));
  Multiplexer #(.select(5), .width(2)) multiplexer_13 (
    .in0(2'b00), .in1(2'b00), .in2(2'b00), .in3(2'b00), .in4(2'b00), .in5(2'b00), .in6(2'b01), .in7(2'b01),
    .in8(2'b10), .in9(2'b00), .in10(2'b00), .in11(2'b00), .in12(2'b00), .in13(2'b00), .in14(2'b00),
    .in15(2'b00), .in16(2'b00), .in17(2'b00), .in18(2'b00), .in19(2'b00), .in20(2'b00), .in21(2'b00),
    .in22(2'b00), .in23(2'b10), .in24(2'b10), .in25(2'b00), .in26(2'b11), .in27(2'b10), .in28(2'b00),
    .in29(2'b00), .in30(2'b00), .in31(2'b00), .out(ALUSrcA), .sel(Selector));
  or or_12 (NOP, comparator_50_eq, and_9_out, and_10_out);
  Multiplexer #(.select(5), .width(2)) multiplexer_14 (
    .in0(2'b00), .in1(2'b00), .in2(2'b00), .in3(2'b00), .in4(2'b11), .in5(2'b00), .in6(2'b00), .in7(2'b00),
    .in8(2'b00), .in9(2'b00), .in10(2'b00), .in11(2'b00), .in12(2'b00), .in13(2'b11), .in14(2'b00),
    .in15(2'b00), .in16(2'b00), .in17(2'b00), .in18(2'b00), .in19(2'b00), .in20(2'b01), .in21(2'b00),
    .in22(2'b00), .in23(2'b10), .in24(2'b10), .in25(2'b10), .in26(2'b10), .in27(2'b10), .in28(2'b11),
    .in29(2'b11), .in30(2'b00), .in31(2'b10), .out(ImmSrc), .sel(Selector));
  Multiplexer #(.select(5), .width(3)) multiplexer_15 (
    .in0(3'b000), .in1(3'b000), .in2(3'b000), .in3(3'b000), .in4(3'b000), .in5(3'b000), .in6(3'b000),
    .in7(3'b000), .in8(3'b101), .in9(3'b000), .in10(3'b000), .in11(3'b101), .in12(3'b101), .in13(3'b010),
    .in14(3'b000), .in15(3'b000), .in16(3'b100), .in17(3'b000), .in18(3'b000), .in19(3'b000), .in20(3'b000),
    .in21(3'b000), .in22(3'b000), .in23(3'b000), .in24(3'b001), .in25(3'b000), .in26(3'b000), .in27(3'b011),
    .in28(3'b000), .in29(3'b000), .in30(3'b000), .in31(3'b000), .out(RegSrc), .sel(Selector));
  Multiplexer #(.select(5), .width(3)) multiplexer_16 (
    .in0(3'b001), .in1(3'b001), .in2(3'b001), .in3(3'b001), .in4(3'b001), .in5(3'b001), .in6(3'b010),
    .in7(3'b010), .in8(3'b010), .in9(3'b001), .in10(3'b001), .in11(3'b001), .in12(3'b001), .in13(3'b001),
    .in14(3'b001), .in15(3'b011), .in16(3'b001), .in17(3'b001), .in18(3'b001), .in19(3'b001), .in20(3'b001),
    .in21(3'b001), .in22(3'b010), .in23(3'b000), .in24(3'b000), .in25(3'b000), .in26(3'b000), .in27(3'b000),
    .in28(3'b001), .in29(3'b001), .in30(3'b100), .in31(3'b000), .out(ALUSrcB), .sel(Selector));
  or or_13 (DualRegWrite, IsRARB, IsRCRD);
  not not_5 (not_5_out, Instr[8]);
  and and_12 (Carry, not_5_out, IsAdd_Sub);
  Multiplexer #(.select(5), .width(3)) multiplexer_17 (
    .in0(3'b000), .in1(3'b000), .in2(3'b000), .in3(3'b000), .in4(3'b001), .in5(3'b000), .in6(3'b000),
    .in7(3'b000), .in8(3'b000), .in9(3'b000), .in10(3'b000), .in11(3'b000), .in12(3'b000), .in13(3'b001),
    .in14(3'b000), .in15(3'b001), .in16(3'b001), .in17(3'b000), .in18(3'b000), .in19(3'b000), .in20(3'b000),
    .in21(3'b010), .in22(3'b000), .in23(3'b011), .in24(3'b011), .in25(3'b011), .in26(3'b011), .in27(3'b011),
    .in28(3'b100), .in29(3'b100), .in30(3'b000), .in31(3'b011), .out(PCSrc_t), .sel(Selector));
  Multiplexer #(.select(5), .width(2)) multiplexer_18 (
    .in0(2'b00), .in1(2'b00), .in2(2'b00), .in3(2'b00), .in4(2'b00), .in5(2'b00), .in6(2'b00), .in7(2'b00),
    .in8(2'b00), .in9(2'b00), .in10(2'b00), .in11(2'b00), .in12(2'b00), .in13(2'b00), .in14(2'b00),
    .in15(2'b00), .in16(2'b00), .in17(2'b00), .in18(2'b00), .in19(2'b00), .in20(2'b00), .in21(2'b01),
    .in22(2'b00), .in23(2'b00), .in24(2'b00), .in25(2'b00), .in26(2'b00), .in27(2'b00), .in28(2'b00),
    .in29(2'b10), .in30(2'b00), .in31(2'b00), .out(TEMPSrc), .sel(Selector));
  Multiplexer #(.select(5)) multiplexer_19 (
    .in0(1'b0), .in1(1'b0), .in2(1'b0), .in3(1'b0), .in4(1'b0), .in5(1'b0), .in6(1'b0), .in7(1'b0),
    .in8(1'b0), .in9(1'b0), .in10(1'b0), .in11(1'b0), .in12(1'b0), .in13(1'b0), .in14(1'b0), .in15(1'b0),
    .in16(1'b0), .in17(1'b0), .in18(1'b0), .in19(1'b0), .in20(1'b0), .in21(1'b1), .in22(1'b0), .in23(1'b0),
    .in24(1'b0), .in25(1'b0), .in26(1'b0), .in27(1'b0), .in28(1'b0), .in29(1'b1), .in30(1'b0), .in31(1'b0),
    .out(TEMPWrite), .sel(Selector));

  assign RotSrc = Instr[9:8];

  // Other names for the same wires on the sheet: CarryEnable = Carry; instr7_4[3:0] = Instr[7:4];
  //   opcode[7:0] = Instr[15:8]; opcode0 = Instr[8]; opcode1_0[1:0] = Instr[9:8]; opcode3_1[2:0] = Instr[11:9];
  //   opcode7_1[6:0] = Instr[15:9]; opcode4_3[1:0] = Instr[12:11]; opcode7_3[4:0] = Instr[15:11];
  //   opcode7_4[3:0] = Instr[15:12]; opcode7_5[2:0] = Instr[15:13]; IsHalt = Halt; IsNOP = NOP;
  //   PCNextSrc[2:0] = PCSrc
endmodule

module instrlengthdec (
  input  [7:0] instr,
  output is2Byte
);

  wire and_1_out, and_2_out, and_3_out, comparator_1_eq, comparator_2_gt, comparator_3_lt, comparator_4_eq,
       comparator_5_gt, comparator_6_lt, comparator_7_gt, comparator_8_lt, comparator_9_gt;

  Comparator #(.mode("unsigned")) comparator_1 (.a(instr), .b(8'h37), .eq(comparator_1_eq));  // open: gt, lt
  Comparator #(.mode("unsigned")) comparator_2 (.a(instr), .b(8'h3f), .gt(comparator_2_gt));  // open: eq, lt
  Comparator #(.mode("unsigned")) comparator_3 (.a(instr), .b(8'h45), .lt(comparator_3_lt));  // open: gt, eq
  Comparator #(.mode("unsigned")) comparator_4 (.a(instr), .b(8'h46), .eq(comparator_4_eq));  // open: gt, lt
  Comparator #(.mode("unsigned")) comparator_5 (.a(instr), .b(8'h4f), .gt(comparator_5_gt));  // open: eq, lt
  Comparator #(.mode("unsigned")) comparator_6 (.a(instr), .b(8'h70), .lt(comparator_6_lt));  // open: gt, eq
  Comparator #(.mode("unsigned")) comparator_7 (.a(instr), .b(8'h7f), .gt(comparator_7_gt));  // open: eq, lt
  Comparator #(.mode("unsigned")) comparator_8 (.a(instr), .b(8'hd0), .lt(comparator_8_lt));  // open: gt, eq
  Comparator #(.mode("unsigned")) comparator_9 (.a(instr), .b(8'hd7), .gt(comparator_9_gt));  // open: eq, lt
  and and_1 (and_1_out, comparator_2_gt, comparator_3_lt);
  and and_2 (and_2_out, comparator_5_gt, comparator_6_lt);
  and and_3 (and_3_out, comparator_7_gt, comparator_8_lt);
  or or_1 (is2Byte, comparator_1_eq, and_1_out, comparator_4_eq, and_2_out, and_3_out, comparator_9_gt);

  // Other names for the same wires on the sheet: opcode[7:0] = instr
endmodule

module regfile (
  input  [2:0] A1,
  input  [2:0] A2,
  input  [2:0] A3,
  input  [3:0] WD,
  input  WE,
  input  [11:0] DualWD,
  input  DualWE,
  input  CLK,
  output [3:0] ReadData,
  output [7:0] RB_RA,
  output [7:0] RD_RC
);

  wire or_1_out, or_2_out, or_3_out, or_4_out, w0, w1, w2, w3, w4, wr0, wr0_1, wr1, wr1_1, wr2, wr2_1, wr3,
       wr3_1, wr4, wr4_1;
  wire [3:0] o2, WD_1, WD_2;

  Decoder #(.select(3)) decoder_1 (
    .out0(wr0), .out1(wr1), .out2(wr2), .out3(wr3), .out4(wr4), .sel(A2));  // open: out5, out6, out7, en
  Decoder #(.select(3)) decoder_2 (
    .out0(wr0_1), .out1(wr1_1), .out2(wr2_1), .out3(wr3_1), .out4(wr4_1), .sel(A3), .en(DualWE));  // open: out5, out6, out7
  Register #(.width(4)) RA (.D(WD_1), .en(w0), .clk(CLK), .Q(RB_RA[3:0]));  // open: clr
  Register #(.width(4)) RB (.D(WD_2), .en(w1), .clk(CLK), .Q(RB_RA[7:4]));  // open: clr
  Register #(.width(4)) RC (.D(WD_1), .en(w2), .clk(CLK), .Q(o2));  // open: clr
  Register #(.width(4)) RD (.D(WD_2), .en(w3), .clk(CLK), .Q(RD_RC[3:0]));  // open: clr
  Register #(.width(4)) RE (.D(WD), .en(w4), .clk(CLK), .Q(RD_RC[7:4]));  // open: clr
  or or_1 (or_1_out, wr0, wr0_1);
  or or_2 (or_2_out, wr1, wr1_1);
  or or_3 (or_3_out, wr2, wr2_1);
  or or_4 (or_4_out, wr2, wr2_1);
  and and_1 (w4, wr4, WE);
  and and_2 (w0, or_1_out, WE);
  and and_3 (w1, or_2_out, WE);
  and and_4 (w2, or_3_out, WE);
  and and_5 (w3, or_4_out, WE);
  // Probe on DualWD[3:0]
  // Probe on DualWD[11:8]
  Multiplexer #(.select(3), .width(4)) multiplexer_1 (
    .in0(RB_RA[3:0]), .in1(RB_RA[7:4]), .in2(o2), .in3(RD_RC[3:0]), .in4(RD_RC[7:4]), .out(ReadData), .sel(A1));  // open: in5, in6, in7
  // Probe on RB_RA
  // Probe on RD_RC
  Multiplexer #(.width(4)) multiplexer_2 (.in0(WD), .in1(DualWD[11:8]), .out(WD_1), .sel(DualWE));
  Multiplexer #(.width(4)) multiplexer_3 (.in0(WD), .in1(DualWD[3:0]), .out(WD_2), .sel(DualWE));

  // Other names for the same wires on the sheet: Y[3:0] = DualWD[3:0]; X[3:0] = DualWD[11:8]; o0[3:0] = RB_RA[3:0];
  //   RBRA[7:0] = RB_RA; o1[3:0] = RB_RA[7:4]; RD[3:0] = ReadData; o3[3:0] = RD_RC[3:0]; RDRC[7:0] = RD_RC;
  //   o4[3:0] = RD_RC[7:4]
endmodule

module alu (
  input  [3:0] SrcA,
  input  [3:0] SrcB,
  input  [2:0] ALUControl,
  input  CarryIn,
  input  CarryEnable,
  output Zero,
  output [3:0] ALUResult,
  output CarryOut
);

  wire b_out, c_in, c_out, or_2_out;
  wire [3:0] adder_1_out, adder_2_out, and_1_out, or_1_out, subtractor_1_out, subtractor_2_out, xor_1_out;

  // Probe on SrcA
  // Probe on SrcB
  Multiplexer multiplexer_1 (.in0(1'b0), .in1(CarryIn), .out(c_in), .sel(CarryEnable));
  Adder #(.width(4)) adder_1 (.a(SrcA), .b(SrcB), .out(adder_1_out), .cin(c_in), .cout(c_out));
  Subtractor #(.width(4)) subtractor_1 (.a(SrcA), .b(SrcB), .out(subtractor_1_out), .bin(CarryIn), .bout(b_out));
  Adder #(.width(4)) adder_2 (.a(SrcA), .b(4'b0001), .out(adder_2_out));  // open: cin, cout
  Subtractor #(.width(4)) subtractor_2 (.a(SrcB), .b(4'b0001), .out(subtractor_2_out));  // open: bin, bout
  assign and_1_out = SrcA & SrcB;  // AND_Gate and_1, 4 bits wide
  assign xor_1_out = SrcA ^ SrcB;  // XOR_Gate xor_1, 4 bits wide
  assign or_1_out = SrcA | SrcB;  // OR_Gate or_1, 4 bits wide
  Multiplexer #(.enable("true"), .select(3), .width(4)) multiplexer_2 (
    .in0(adder_1_out), .in1(subtractor_1_out), .in2(adder_2_out), .in3(subtractor_2_out), .in4(and_1_out),
    .in5(xor_1_out), .in6(or_1_out), .out(ALUResult), .sel(ALUControl));  // open: in7, en
  // Probe on ALUControl
  // Probe on ALUResult
  Multiplexer multiplexer_3 (.in0(c_out), .in1(b_out), .out(CarryOut), .sel(ALUControl[0]));
  or or_2 (or_2_out, ALUResult[0], ALUResult[1], ALUResult[3], ALUResult[2]);
  not not_1 (Zero, or_2_out);

  // Other names for the same wires on the sheet: cf = CarryIn; cf_enable = CarryEnable

  // Notes on the sheet:
  //   Input
  //   ALUResult
  //   Output
  //   Zero
endmodule

module aludec (
  input  [7:0] opcode,
  output [2:0] ALUControl
);

  wire and_1_out, comparator_1_eq, comparator_2_eq, comparator_3_eq, comparator_4_eq, comparator_5_eq,
       comparator_6_eq, comparator_7_eq, comparator_8_gt, comparator_9_lt, comparator_10_eq,
       comparator_11_eq, comparator_12_eq, comparator_13_eq, comparator_14_eq, comparator_15_eq,
       comparator_16_eq, comparator_17_eq, comparator_18_eq, comparator_19_eq, comparator_20_eq,
       comparator_21_eq, comparator_22_eq, comparator_23_eq, comparator_24_eq, comparator_25_eq,
       comparator_26_eq, comparator_27_eq, IsAdd, IsAND, IsDec, IsInc, IsOR, IsSub, IsXOR;

  Comparator comparator_1 (.a(opcode), .b(8'h8), .eq(comparator_1_eq));  // open: gt, lt
  Comparator comparator_2 (.a(opcode), .b(8'h9), .eq(comparator_2_eq));  // open: gt, lt
  Comparator comparator_3 (.a(opcode), .b(8'h40), .eq(comparator_3_eq));  // open: gt, lt
  Comparator comparator_4 (.a(opcode), .b(8'h36), .eq(comparator_4_eq));  // open: gt, lt
  Comparator comparator_5 (.a(opcode), .b(8'ha), .eq(comparator_5_eq));  // open: gt, lt
  Comparator comparator_6 (.a(opcode), .b(8'hb), .eq(comparator_6_eq));  // open: gt, lt
  Comparator comparator_7 (.a(opcode), .b(8'h41), .eq(comparator_7_eq));  // open: gt, lt
  Comparator #(.mode("unsigned"), .width(5)) comparator_8 (
    .a(opcode[7:3]), .b(5'b10011), .gt(comparator_8_gt));  // open: eq, lt
  Comparator #(.mode("unsigned"), .width(5)) comparator_9 (
    .a(opcode[7:3]), .b(5'b11010), .lt(comparator_9_lt));  // open: gt, eq
  Comparator #(.mode("unsigned"), .width(5)) comparator_10 (
    .a(opcode[7:3]), .b(5'b11011), .eq(comparator_10_eq));  // open: gt, lt
  and and_1 (and_1_out, comparator_8_gt, comparator_9_lt);
  or or_1 (IsAdd, comparator_1_eq, comparator_2_eq, comparator_3_eq, comparator_4_eq);
  or or_2 (IsSub, comparator_5_eq, comparator_6_eq, comparator_7_eq, and_1_out, comparator_10_eq);
  Priority_Encoder priority_encoder_1 (
    .in0(IsAdd), .in1(IsSub), .in2(IsInc), .in3(IsDec), .in4(IsAND), .in5(IsXOR), .in6(IsOR), .out(ALUControl));  // open: in7, en_in, gs, en_out
  Comparator comparator_11 (.a(opcode), .b(8'h1a), .eq(comparator_11_eq));  // open: gt, lt
  Comparator comparator_12 (.a(opcode), .b(8'h1d), .eq(comparator_12_eq));  // open: gt, lt
  Comparator comparator_13 (.a(opcode), .b(8'h42), .eq(comparator_13_eq));  // open: gt, lt
  Comparator comparator_14 (.a(opcode), .b(8'h1b), .eq(comparator_14_eq));  // open: gt, lt
  Comparator comparator_15 (.a(opcode), .b(8'h1e), .eq(comparator_15_eq));  // open: gt, lt
  Comparator comparator_16 (.a(opcode), .b(8'h43), .eq(comparator_16_eq));  // open: gt, lt
  Comparator comparator_17 (.a(opcode), .b(8'h1c), .eq(comparator_17_eq));  // open: gt, lt
  Comparator comparator_18 (.a(opcode), .b(8'h1f), .eq(comparator_18_eq));  // open: gt, lt
  Comparator comparator_19 (.a(opcode), .b(8'h44), .eq(comparator_19_eq));  // open: gt, lt
  or or_3 (IsAND, comparator_11_eq, comparator_12_eq, comparator_13_eq);
  or or_4 (IsXOR, comparator_14_eq, comparator_15_eq, comparator_16_eq);
  or or_5 (IsOR, comparator_17_eq, comparator_18_eq, comparator_19_eq);
  Comparator comparator_20 (.a(opcode), .b(8'hc), .eq(comparator_20_eq));  // open: gt, lt
  Comparator comparator_21 (.a(opcode), .b(8'he), .eq(comparator_21_eq));  // open: gt, lt
  Comparator #(.width(5)) comparator_22 (
    .a({opcode[7:4], opcode[0]}), .b(5'b00010), .eq(comparator_22_eq));  // open: gt, lt
  Comparator comparator_23 (.a(opcode), .b(8'h31), .eq(comparator_23_eq));  // open: gt, lt
  Comparator comparator_24 (.a(opcode), .b(8'hd), .eq(comparator_24_eq));  // open: gt, lt
  Comparator comparator_25 (.a(opcode), .b(8'hf), .eq(comparator_25_eq));  // open: gt, lt
  Comparator #(.width(5)) comparator_26 (
    .a({opcode[7:4], opcode[0]}), .b(5'b00011), .eq(comparator_26_eq));  // open: gt, lt
  Comparator comparator_27 (.a(opcode), .b(8'h3f), .eq(comparator_27_eq));  // open: gt, lt
  or or_6 (IsInc, comparator_20_eq, comparator_21_eq, comparator_22_eq, comparator_23_eq);
  or or_7 (IsDec, comparator_24_eq, comparator_25_eq, comparator_26_eq, comparator_27_eq);

  // Other names for the same wires on the sheet: concat[4:0] = {opcode[7:4], opcode[0]}; opcode_0 = opcode[0];
  //   funct[3:0] = opcode[7:4]; functb[4:0] = opcode[7:3]

  // Notes on the sheet:
  //   instr[7:4|0]
endmodule

module datamem (
  input  [7:0] A,
  input  WE,
  input  [3:0] WD,
  input  clk,
  output [3:0] RD
);

  RAM #(.asyncread("true"), .dataWidth(4)) ram_1 (.addr(A), .we(WE), .oe(1'b1), .clk(clk), .din(WD), .dout(RD));

  // Other names for the same wires on the sheet: WriteData[3:0] = WD; WriteEnable = WE
endmodule

module immdec (
  input  [15:0] Instr,
  input  [1:0] ImmSrc,
  output [11:0] Imm11_0
);

  wire [11:0] bit_extender_1_out, bit_extender_2_out, bit_extender_3_out;

  assign bit_extender_1_out = {{8{1'b0}}, Instr[3:0]};  // Bit_Extender bit_extender_1
  assign bit_extender_2_out = {{8{1'b0}}, Instr[11:8]};  // Bit_Extender bit_extender_2
  assign bit_extender_3_out = {{1{1'b0}}, Instr[10:0]};  // Bit_Extender bit_extender_3
  Multiplexer #(.select(2), .width(12)) multiplexer_1 (
    .in0(bit_extender_1_out), .in1(bit_extender_2_out), .in2(bit_extender_3_out), .in3(Instr[11:0]),
    .out(Imm11_0), .sel(ImmSrc));

  // Other names for the same wires on the sheet: ALU_R4Imm[3:0] = Instr[3:0]; BImm[11:0] = Instr[11:0];
  //   BranchImm[10:0] = Instr[10:0]; ACCImm[3:0] = Instr[11:8]
endmodule

module instrmem (
  input  [15:0] A1,
  input  [15:0] A2,
  output [7:0] instr1,
  output [7:0] Instr2
);

  ROM #(.addrWidth(16)) InstructionMemory (.addr(A1), .data(instr1));
  ROM #(.addrWidth(16)) rom_1 (.addr(A2), .data(Instr2));

  // Notes on the sheet:
  //   contents of InstructionMemory (hex, n*v repeats v):
  //   37 3e f3 16
  //   contents of rom_1 (hex, n*v repeats v):
  //   37 3e f3 16
endmodule

module rotate (
  input  [3:0] ACCIn,
  input  cfIn,
  input  [1:0] RotSrc,
  output [3:0] accOut
);

  // Probe on ACCIn
  // Probe on ACCIn
  // Probe on ACCIn
  // Probe on ACCIn
  // Probe on {ACCIn[2:0], ACCIn[3]}
  // Probe on {ACCIn[0], ACCIn[3:1]}
  // Probe on {ACCIn[2:0], cfIn}
  // Probe on {cfIn, ACCIn[3:1]}
  Multiplexer #(.select(2), .width(4)) multiplexer_1 (
    .in0({ACCIn[0], ACCIn[3:1]}), .in1({ACCIn[2:0], ACCIn[3]}), .in2({cfIn, ACCIn[3:1]}),
    .in3({ACCIn[2:0], cfIn}), .out(accOut), .sel(RotSrc));

  // Other names for the same wires on the sheet: rotl[3:0] = {ACCIn[2:0], ACCIn[3]}; rotlc[3:0] = {ACCIn[2:0], cfIn};
  //   rotr[3:0] = {ACCIn[0], ACCIn[3:1]}; rotrc[3:0] = {cfIn, ACCIn[3:1]}; RotSel[1:0] = RotSrc
endmodule

module dualreg (
  input  IsRARB,
  input  IsRCRD,
  input  DualRegSrc,
  input  [11:0] Imm
);

  wire [3:0] undriven, undriven_2, wda;

  Multiplexer #(.width(4)) multiplexer_1 (.in0(undriven), .in1(undriven_2), .out(wda));  // open: sel

  // Other names for the same wires on the sheet: Y[3:0] = Imm[3:0]; X[3:0] = Imm[11:8]; Src = DualRegSrc
endmodule
